# Fritzing sketch clock_circuit (saved by Fritzing 0.9.1b)
perfboards: 1

parts:
  Part1 = Arduino Nano (Rev3.0)
  R1 = Resistor [tolerance=±5% resistance=470 package=THT]
  NEOPIXEL1 = Neopixel Strip -- Black (60/m)
  Part2 = Real Time Clock Module - DS1307 RTC Breakout Board
  C1 = Electrolytic Capacitor [capacitance=1000µF package="300 mil [THT, electrolytic]"]
  JACK1 = 2.1mm Barrel Jack with Terminal Block  # not connected

nets:
  GND: Part1.GND, Part2.GND, C1.-
  N1: Part1.D3, R1.Pin_0
  5V: Part1.5V, Part2.5V, C1.+
  N2: Part1.A5, Part2.SCL
  N3: Part1.A4, Part2.SDA
  N4: R1.Pin_1, NEOPIXEL1.+5V

notes:
  pretend this is a ChronoDot...

custom parts:
  Neopixel Strip -- Black (60/m): Neopixel Strip, Black, 60 pixels per meter.
